// Logisim project asac.circ as structural Verilog: 5 circuits, main circuit audio_output
module main (
);

  wire and_1_out, clock_1_out, comparator_1_eq, comparator_2_eq, demultiplexer_1_out0, demultiplexer_1_out1,
       demultiplexer_1_out2, demultiplexer_1_out4;
  wire [2:0] Microcode_data;
  wire [7:0] Program_data;
  wire [7:3] Microcode_data_2;
  wire [15:0] PC_q, Program_data_2;
  wire [31:24] Program_data_3;

  Clock clock_1 (.out(clock_1_out));
  Counter #(.max('hffff), .width(16)) PC (
    .load(comparator_1_eq), .clk(clock_1_out), .D(Program_data_2), .Q(PC_q));  // open: clr, up, count, carry
  Comparator comparator_1 (.a({Microcode_data_2, Microcode_data}), .b(8'h42), .eq(comparator_1_eq));  // open: gt, lt
  ROM #(.addrWidth(16), .dataWidth(32)) Program (.addr(PC_q), .data({Program_data_3, Program_data_2, Program_data}));
  // Probe on Program_data
  ROM Microcode (.addr(Program_data), .data({Microcode_data_2, Microcode_data}));
  LED led_1 (.in(demultiplexer_1_out0));
  LED led_2 (.in(demultiplexer_1_out1));
  Demultiplexer #(.select(3)) demultiplexer_1 (
    .out0(demultiplexer_1_out0), .out1(demultiplexer_1_out1), .out2(demultiplexer_1_out2),
    .out4(demultiplexer_1_out4), .in(and_1_out), .sel(Microcode_data));  // open: out3, out5, out6, out7
  and and_1 (and_1_out, Microcode_data_2[5], Microcode_data_2[3]);
  // Probe on {Microcode_data_2, Microcode_data}
  LED led_3 (.in(demultiplexer_1_out2));
  LED led_4 (.in(demultiplexer_1_out4));
  channel channel_1 (
    .Addr(Program_data_2[7:0]), .v(Program_data_2[15:8]), .E(demultiplexer_1_out4), .Clk(clock_1_out),
    .W(2'b11));
  Comparator comparator_2 (.a({Microcode_data_2, Microcode_data}), .b(8'hde), .eq(comparator_2_eq));  // open: gt, lt
  // Probe on Program_data_2[15:8]
  channel channel_2 (
    .Addr(Program_data_2[7:0]), .v(Program_data_2[15:8]), .E(demultiplexer_1_out2), .Clk(clock_1_out),
    .W(2'b10));
  LED led_5 (.in(comparator_2_eq));
  // Probe on Program_data_2[7:0]
  channel channel_3 (
    .Addr(Program_data_2[7:0]), .v(Program_data_2[15:8]), .E(demultiplexer_1_out1), .Clk(clock_1_out),
    .W(2'b01));
  channel channel_4 (
    .Addr(Program_data_2[7:0]), .v(Program_data_2[15:8]), .E(demultiplexer_1_out0), .Clk(clock_1_out),
    .W(2'b00));

  // Notes on the sheet:
  //   contents of Program (hex, n*v repeats v):
  //   644104 8 8 4100 644205 8 8 4201 644306 8 8 4302 644407 8 8 4403 9
  //   contents of Microcode (hex, n*v repeats v):
  //   28 29 2a 2c 38 39 3a 3c de 42
endmodule

module audio_output (
  input  [15:0] f,
  input  [7:0] v,
  input  Clk,
  input  E,
  input  [1:0] W
);

  wire demultiplexer_1_out0, demultiplexer_1_out1, demultiplexer_1_out2, demultiplexer_1_out3, register_1_q;
  wire [7:0] Vol_q;
  wire [15:0] Freq_q;

  Register #(.width(16)) Freq (.D(f), .en(E), .clk(Clk), .Q(Freq_q));  // open: clr
  Register #(.width(1)) register_1 (.D(E), .en(E), .clk(Clk), .Q(register_1_q));  // open: clr
  Register Vol (.D(v), .en(E), .clk(Clk), .Q(Vol_q));  // open: clr
  Demultiplexer #(.select(2)) demultiplexer_1 (
    .out0(demultiplexer_1_out0), .out1(demultiplexer_1_out1), .out2(demultiplexer_1_out2),
    .out3(demultiplexer_1_out3), .in(register_1_q), .sel(W));
  // Buzzer #(.vol_width(8), .waveform("Square")) Square: pin names not known; wires that end beside it: Freq_q[13:0], demultiplexer_1_out0, Vol_q
  // Buzzer #(.vol_width(8), .waveform("Triangle")) Triangle: pin names not known; wires that end beside it: Freq_q[13:0], demultiplexer_1_out1, Vol_q
  // Buzzer #(.vol_width(8)) Sine: pin names not known; wires that end beside it: Freq_q[13:0], demultiplexer_1_out2, Vol_q
  // Buzzer #(.vol_width(8), .waveform("Sawtooth")) SawTooth: pin names not known; wires that end beside it: Freq_q[13:0], demultiplexer_1_out3, Vol_q
endmodule

module output_unit (
  input  [15:0] f,
  input  [7:0] v,
  input  [4:0] Sel,
  input  E,
  input  Clk,
  input  [1:0] W
);

  wire decoder_1_out0, decoder_1_out1, decoder_1_out2, decoder_1_out3, decoder_1_out4, decoder_1_out5,
       decoder_1_out6, decoder_1_out7, decoder_1_out8, decoder_1_out9, decoder_1_out10, decoder_1_out11,
       decoder_1_out12, decoder_1_out13, decoder_1_out14, decoder_1_out15, decoder_1_out16, decoder_1_out17,
       decoder_1_out18, decoder_1_out19, decoder_1_out20, decoder_1_out21, decoder_1_out22, decoder_1_out23,
       decoder_1_out24, decoder_1_out26, decoder_1_out27, decoder_1_out28, decoder_1_out29, decoder_1_out30,
       decoder_1_out31;

  audio_output audio_output_1 (.f(f), .v(v), .Clk(Clk), .E(decoder_1_out0), .W(W));
  audio_output audio_output_2 (.f(f), .v(v), .Clk(Clk), .E(decoder_1_out1), .W(W));
  audio_output audio_output_3 (.f(f), .v(v), .Clk(Clk), .E(decoder_1_out2), .W(W));
  audio_output audio_output_4 (.f(f), .v(v), .Clk(Clk), .E(decoder_1_out3), .W(W));
  audio_output audio_output_5 (.f(f), .v(v), .Clk(Clk), .E(decoder_1_out4), .W(W));
  audio_output audio_output_6 (.f(f), .v(v), .Clk(Clk), .E(decoder_1_out5), .W(W));
  audio_output audio_output_7 (.f(f), .v(v), .Clk(Clk), .E(decoder_1_out6), .W(W));
  audio_output audio_output_8 (.f(f), .v(v), .Clk(Clk), .E(decoder_1_out7), .W(W));
  Decoder #(.select(5)) decoder_1 (
    .out0(decoder_1_out0), .out1(decoder_1_out1), .out2(decoder_1_out2), .out3(decoder_1_out3),
    .out4(decoder_1_out4), .out5(decoder_1_out5), .out6(decoder_1_out6), .out7(decoder_1_out7),
    .out8(decoder_1_out8), .out9(decoder_1_out9), .out10(decoder_1_out10), .out11(decoder_1_out11),
    .out12(decoder_1_out12), .out13(decoder_1_out13), .out14(decoder_1_out14), .out15(decoder_1_out15),
    .out16(decoder_1_out16), .out17(decoder_1_out17), .out18(decoder_1_out18), .out19(decoder_1_out19),
    .out20(decoder_1_out20), .out21(decoder_1_out21), .out22(decoder_1_out22), .out23(decoder_1_out23),
    .out24(decoder_1_out24), .out25(decoder_1_out24), .out26(decoder_1_out26), .out27(decoder_1_out27),
    .out28(decoder_1_out28), .out29(decoder_1_out29), .out30(decoder_1_out30), .out31(decoder_1_out31),
    .sel(Sel), .en(E));
  audio_output audio_output_9 (.f(f), .v(v), .Clk(Clk), .E(decoder_1_out8), .W(W));
  audio_output audio_output_10 (.f(f), .v(v), .Clk(Clk), .E(decoder_1_out9), .W(W));
  audio_output audio_output_11 (.f(f), .v(v), .Clk(Clk), .E(decoder_1_out10), .W(W));
  audio_output audio_output_12 (.f(f), .v(v), .Clk(Clk), .E(decoder_1_out11), .W(W));
  audio_output audio_output_13 (.f(f), .v(v), .Clk(Clk), .E(decoder_1_out12), .W(W));
  audio_output audio_output_14 (.f(f), .v(v), .Clk(Clk), .E(decoder_1_out13), .W(W));
  audio_output audio_output_15 (.f(f), .v(v), .Clk(Clk), .E(decoder_1_out14), .W(W));
  audio_output audio_output_16 (.f(f), .v(v), .Clk(Clk), .E(decoder_1_out15), .W(W));
  audio_output audio_output_17 (.f(f), .v(v), .Clk(Clk), .E(decoder_1_out16), .W(W));
  audio_output audio_output_18 (.f(f), .v(v), .Clk(Clk), .E(decoder_1_out17), .W(W));
  audio_output audio_output_19 (.f(f), .v(v), .Clk(Clk), .E(decoder_1_out18), .W(W));
  audio_output audio_output_20 (.f(f), .v(v), .Clk(Clk), .E(decoder_1_out19), .W(W));
  audio_output audio_output_21 (.f(f), .v(v), .Clk(Clk), .E(decoder_1_out20), .W(W));
  audio_output audio_output_22 (.f(f), .v(v), .Clk(Clk), .E(decoder_1_out21), .W(W));
  audio_output audio_output_23 (.f(f), .v(v), .Clk(Clk), .E(decoder_1_out22), .W(W));
  audio_output audio_output_24 (.f(f), .v(v), .Clk(Clk), .E(decoder_1_out23), .W(W));
  audio_output audio_output_25 (.f(f), .v(v), .Clk(Clk), .E(decoder_1_out24), .W(W));
  audio_output audio_output_26 (.f(f), .v(v), .Clk(Clk), .E(decoder_1_out24), .W(W));
  audio_output audio_output_27 (.f(f), .v(v), .Clk(Clk), .E(decoder_1_out26), .W(W));
  audio_output audio_output_28 (.f(f), .v(v), .Clk(Clk), .E(decoder_1_out27), .W(W));
  audio_output audio_output_29 (.f(f), .v(v), .Clk(Clk), .E(decoder_1_out28), .W(W));
  audio_output audio_output_30 (.f(f), .v(v), .Clk(Clk), .E(decoder_1_out29));  // open: W
  audio_output audio_output_31 (.f(f), .v(v), .Clk(Clk), .E(decoder_1_out30), .W(W));
  audio_output audio_output_32 (.f(f), .v(v), .Clk(Clk), .E(decoder_1_out31), .W(W));
endmodule

module channel (
  input  [7:0] Addr,
  input  [7:0] v,
  input  E,
  input  Clk,
  input  [1:0] W
);

  wire demultiplexer_1_out0, demultiplexer_1_out1, demultiplexer_1_out2, demultiplexer_1_out3;
  wire [7:0] mod32_1_m, mod32_1_r;
  wire [15:0] LUT_f_data;

  mod32 mod32_1 (.Addr(Addr), .M(mod32_1_m), .R(mod32_1_r));
  Demultiplexer #(.select(2)) demultiplexer_1 (
    .out0(demultiplexer_1_out0), .out1(demultiplexer_1_out1), .out2(demultiplexer_1_out2),
    .out3(demultiplexer_1_out3), .in(E), .sel(mod32_1_r[1:0]));
  output_unit c0_31 (.f(LUT_f_data), .v(v), .Sel(mod32_1_m[4:0]), .E(demultiplexer_1_out0), .Clk(Clk), .W(W));
  output_unit output_unit_1 (.f(LUT_f_data), .v(v), .Sel(mod32_1_m[4:0]), .E(demultiplexer_1_out1), .Clk(Clk), .W(W));
  output_unit c64_95 (.f(LUT_f_data), .v(v), .Sel(mod32_1_m[4:0]), .E(demultiplexer_1_out2), .Clk(Clk), .W(W));
  output_unit c96_127 (.f(LUT_f_data), .v(v), .Sel(mod32_1_m[4:0]), .E(demultiplexer_1_out3), .Clk(Clk), .W(W));
  ROM #(.dataWidth(16)) LUT_f (.addr(Addr), .data(LUT_f_data));

  // Notes on the sheet:
  //   contents of LUT_f (hex, n*v repeats v):
  //   8 9 9 a a b c c d e f f 10 11 12 13 15 16 17 18 1a 1c 1d 1f 21 23 25 27 29 2c 2e 31 34 37 3a 3e 41
  //   45 49 4e 52 57 5c 62 68 6e 75 7b 83 8b 93 9c a5 af b9 c4 d0 dc e9 f7 106 115 126 137 14a 15d 172 188
  //   19f 1b8 1d2 1ee 20b 22a 24b 26e 293 2ba 2e4 310 33f 370 3a4 3dc 417 455 497 4dd 527 575 5c8 620 67d
  //   6e0 749 7b8 82d 8a9 92d 9b9 a4d aea b90 c40 cfa dc0 e91 f6f 105a 1153 125b 1372 149a 15d4 1720 1880
  //   19f5 1b80 1d23 1ede 20b4 22a6 24b5 26e4 2934 2ba7 2e40 3100
endmodule

module mod32 (
  input  [7:0] Addr,
  output [7:0] M,
  output [7:0] R
);

  wire [7:0] multiplier_1_out;

  Divider divider_1 (.a(Addr), .b(8'h20), .out(M));  // open: upper, rem
  Multiplier multiplier_1 (.a(M), .b(8'h20), .out(multiplier_1_out));  // open: cin, cout
  Subtractor subtractor_1 (.a(Addr), .b(multiplier_1_out), .out(R));  // open: bin, bout
  // Probe on R
  // Probe on M
endmodule
